# Fritzing sketch Esquema conexion dht11 (saved by Fritzing 0.7.10b)
breadboards: 1

parts:
  RHT1 = Humidity and Temperature Sensor RHT03
  Arduino1 = Arduino
  R1 = Resistor [tolerance=±5% resistance=5k package=THT]

nets:
  VCC: RHT1.Vcc, Arduino1.+5V, R1.Pin_1
  N1: RHT1.Data-signal, Arduino1.D2, R1.Pin_0
  N2: RHT1.GND_2, Arduino1.GND
